# Fritzing sketch cubo (saved by Fritzing 0.9.3b)
breadboards: 1

parts:
  LED43 = LED - 5mm [color="Green (555nm)" package="5 mm [THT]"]
  LED44 = LED - 5mm [color="Green (555nm)" package="5 mm [THT]"]
  LED45 = LED - 5mm [color="Green (555nm)" package="5 mm [THT]"]
  LED46 = LED - 5mm [color="Green (555nm)" package="5 mm [THT]"]
  LED47 = LED - 5mm [color="Green (555nm)" package="5 mm [THT]"]
  LED48 = LED - 5mm [color="Green (555nm)" package="5 mm [THT]"]
  LED49 = LED - 5mm [color="Green (555nm)" package="5 mm [THT]"]
  LED50 = LED - 5mm [color="Green (555nm)" package="5 mm [THT]"]
  LED51 = LED - 5mm [color="Green (555nm)" package="5 mm [THT]"]
  R1 = Resistor [tolerance=±5% resistance=220 package="2512 [SMD]"]
  R2 = Resistor [tolerance=±5% resistance=220 package="2512 [SMD]"]
  R3 = Resistor [tolerance=±5% resistance=220 package="2512 [SMD]"]
  Q1 = NPN-Transistor [package="TO92 [THT]"]
  R10 = Resistor [tolerance=±5% resistance=220 package="2512 [SMD]"]
  Raspberry_Pi_Zero1 = Raspberry Pi Zero
  LED52 = LED - 5mm [color="Green (555nm)" package="5 mm [THT]"]
  LED53 = LED - 5mm [color="Green (555nm)" package="5 mm [THT]"]
  LED54 = LED - 5mm [color="Green (555nm)" package="5 mm [THT]"]
  LED55 = LED - 5mm [color="Green (555nm)" package="5 mm [THT]"]
  LED56 = LED - 5mm [color="Green (555nm)" package="5 mm [THT]"]
  LED57 = LED - 5mm [color="Green (555nm)" package="5 mm [THT]"]
  LED58 = LED - 5mm [color="Green (555nm)" package="5 mm [THT]"]
  LED59 = LED - 5mm [color="Green (555nm)" package="5 mm [THT]"]
  LED60 = LED - 5mm [color="Green (555nm)" package="5 mm [THT]"]
  R11 = Resistor [tolerance=±5% resistance=220 package="2512 [SMD]"]
  R12 = Resistor [tolerance=±5% resistance=220 package="2512 [SMD]"]
  R13 = Resistor [tolerance=±5% resistance=220 package="2512 [SMD]"]
  R14 = Resistor [tolerance=±5% resistance=220 package="2512 [SMD]"]
  Q2 = NPN-Transistor [package="TO92 [THT]"]
  LED61 = LED - 5mm [color="Green (555nm)" package="5 mm [THT]"]
  LED62 = LED - 5mm [color="Green (555nm)" package="5 mm [THT]"]
  LED63 = LED - 5mm [color="Green (555nm)" package="5 mm [THT]"]
  LED64 = LED - 5mm [color="Green (555nm)" package="5 mm [THT]"]
  LED65 = LED - 5mm [color="Green (555nm)" package="5 mm [THT]"]
  LED66 = LED - 5mm [color="Green (555nm)" package="5 mm [THT]"]
  LED67 = LED - 5mm [color="Green (555nm)" package="5 mm [THT]"]
  LED68 = LED - 5mm [color="Green (555nm)" package="5 mm [THT]"]
  LED69 = LED - 5mm [color="Green (555nm)" package="5 mm [THT]"]
  R15 = Resistor [tolerance=±5% resistance=220 package="2512 [SMD]"]
  R16 = Resistor [tolerance=±5% resistance=220 package="2512 [SMD]"]
  R17 = Resistor [tolerance=±5% resistance=220 package="2512 [SMD]"]
  R18 = Resistor [tolerance=±5% resistance=220 package="2512 [SMD]"]
  Q3 = NPN-Transistor [package="TO92 [THT]"]

nets:
  N1: LED43.cathode, LED44.cathode, LED45.cathode, LED46.cathode, LED47.cathode, LED48.cathode, LED49.cathode, LED50.cathode, LED51.cathode, Q1.E
  N2: LED43.anode, R3.Pin_1, LED54.anode, LED63.anode
  N3: LED44.anode, R2.Pin_1, LED58.anode, LED67.anode
  N4: LED45.anode, R1.Pin_1, LED52.anode, LED61.anode
  N5: LED46.anode, LED59.anode, R13.Pin_1, LED68.anode
  N6: LED47.anode, LED60.anode, R14.Pin_1, LED69.anode
  N7: LED48.anode, LED57.anode, R11.Pin_1, LED66.anode
  N8: LED49.anode, LED53.anode, LED62.anode, R17.Pin_1
  N9: LED50.anode, LED56.anode, LED65.anode, R18.Pin_1
  N10: LED51.anode, LED55.anode, LED64.anode, R15.Pin_1
  N11: R1.Pin_0, Raspberry_Pi_Zero1.GPIO2
  N12: R2.Pin_0, Raspberry_Pi_Zero1.GPIO3
  N13: R3.Pin_0, Raspberry_Pi_Zero1.GPIO18
  N14: Q1.B, R10.Pin_1
  N15: Q1.C, Raspberry_Pi_Zero1.GND, Q2.C, Q3.C
  N16: R10.Pin_0, Raspberry_Pi_Zero1.GPIO17
  N17: Raspberry_Pi_Zero1.GPIO27, R12.Pin_0
  N18: Raspberry_Pi_Zero1.GPIO22, R16.Pin_0
  N19: Raspberry_Pi_Zero1.GPIO10, R11.Pin_0
  N20: Raspberry_Pi_Zero1.GPIO9, R14.Pin_0
  N21: Raspberry_Pi_Zero1.GPIO11, R13.Pin_0
  N22: Raspberry_Pi_Zero1.GPIO7, R17.Pin_0
  N23: Raspberry_Pi_Zero1.GPIO8, R18.Pin_0
  N24: Raspberry_Pi_Zero1.GPIO25, R15.Pin_0
  N25: LED52.cathode, LED53.cathode, LED54.cathode, LED55.cathode, LED56.cathode, LED57.cathode, LED58.cathode, LED59.cathode, LED60.cathode, Q2.E
  N26: R12.Pin_1, Q2.B
  N27: LED61.cathode, LED62.cathode, LED63.cathode, LED64.cathode, LED65.cathode, LED66.cathode, LED67.cathode, LED68.cathode, LED69.cathode, Q3.E
  N28: R16.Pin_1, Q3.B
