# Fritzing sketch simplificado (saved by Fritzing 0.9.3b)
breadboards: 1

parts:
  Q1 = NPN-Transistor [package="TO92 [THT]"]
  PINO_I/O_A = Header 1 [package=pad-1.5x4.5]
  GND1 = Header 1 [package=pad-1.5x4.5]
  PINO_I/O_1 = Header 1 [package=pad-1.5x4.5]
  PINO_I/O_2 = Header 1 [package=pad-1.5x4.5]
  LED12 = LED - 5mm [color="Red (633nm)" package="5 mm [THT]"]
  LED14 = LED - 5mm [color="Red (633nm)" package="5 mm [THT]"]
  LED16 = LED - 5mm [color="Red (633nm)" package="5 mm [THT]"]
  LED18 = LED - 5mm [color="Red (633nm)" package="5 mm [THT]"]
  Q2 = NPN-Transistor [package="TO92 [THT]"]
  GND = Header 1 [package=pad-1.5x4.5]
  PINO_I/O_B = Header 1 [package=pad-1.5x4.5]

nets:
  N1: Q1.E, LED16.cathode, LED18.cathode
  N2: Q1.B, PINO_I/O_A.1
  N3: Q1.C, GND1.1
  N4: PINO_I/O_1.1, LED12.anode, LED16.anode
  N5: PINO_I/O_2.1, LED14.anode, LED18.anode
  N6: LED12.cathode, LED14.cathode, Q2.E
  N7: Q2.B, PINO_I/O_B.1
  N8: Q2.C, GND.1
