# Fritzing sketch lcd (saved by Fritzing 0.9.3b)
breadboards: 1

parts:
  U1 = LCD-16X2 [package=lcd-16x2_noholes]
  Botao_1 = Pushbutton [package="[SMD]"]
  PIR1 = PIR sensor
  PIR2 = PIR sensor
  DHT1 = DHT11 Humitidy and Temperature Sensor
  Raspberry_Pi1 = Raspberry Pi B rev2
  Botao_2 = Pushbutton [package="[SMD]"]
  R1 = Resistor [tolerance=±5% resistance=220 package=THT]
  R2 = Rotary Potentiometer (Small) [maximum_resistance=100kΩ package=THT]

nets:
  GND: U1.VSS, U1.R_W, PIR1.GND, PIR2.GND, DHT1.GND, Raspberry_Pi1.GND, R2.leg1
  VDD: U1.VDD, U1.A, U1.K, Raspberry_Pi1.5V, R2.leg2
  N1: U1.VO, R2.wiper
  N2: U1.RS, Raspberry_Pi1.GPIO_17
  N3: U1.E, Raspberry_Pi1.GPIO_27
  N4: U1.DB4, Raspberry_Pi1.GPIO_22
  N5: U1.DB5, Raspberry_Pi1.GPIO_10
  N6: U1.DB6, Raspberry_Pi1.GPIO_9
  N7: U1.DB7, Raspberry_Pi1.GPIO_11
  N8: Botao_1.Pin_1, Botao_1.Pin_2, Raspberry_Pi1.GPIO_7
  VDD_2: Botao_1.Pin_3, Botao_1.Pin_4, PIR1.VDD, PIR2.VDD, Raspberry_Pi1.3V3, Botao_2.Pin_3, Botao_2.Pin_4, R1.Pin_1
  N9: PIR1.SIG, Raspberry_Pi1.GPIO_23
  N10: PIR2.SIG, Raspberry_Pi1.GPIO_24
  N11: DHT1.VDD, DHT1.DATA, Raspberry_Pi1.GPIO_25, R1.Pin_0
  N12: Raspberry_Pi1.GPIO_8, Botao_2.Pin_1, Botao_2.Pin_2

custom parts:
  DHT11 Humitidy and Temperature Sensor: DHT11 Humidity and Temperature Sensor
