# Fritzing sketch Untitled Sketch (saved by Fritzing 0.9.3b)
breadboards: 1

parts:
  Raspberry_Pi_Zero1 = Raspberry Pi Zero
  4_Channel_Relay1 = 4 Channel Power Relay

nets:
  GND: Raspberry_Pi_Zero1.GND, 4_Channel_Relay1.GND
  N1: Raspberry_Pi_Zero1.GPIO17, 4_Channel_Relay1.IN1
  N2: Raspberry_Pi_Zero1.GPIO27, 4_Channel_Relay1.IN2
  N3: Raspberry_Pi_Zero1.GPIO22, 4_Channel_Relay1.IN3
  N4: Raspberry_Pi_Zero1.GPIO23, 4_Channel_Relay1.IN4
  N5: Raspberry_Pi_Zero1.5V, 4_Channel_Relay1.VCC#13
  N6: 4_Channel_Relay1.VCC#14, 4_Channel_Relay1.JD-VCC

custom parts:
  4 Channel Power Relay: A 4 channel power relay. The module operates at 5V.
