# Fritzing sketch rele (saved by Fritzing 0.9.3b)
breadboards: 1

parts:
  Raspberry_Pi_Zero1 = Raspberry Pi Zero
  4_Channel_Relay1 = 4 Channel Power Relay
  R2 = Resistor [tolerance=±5% resistance=220 package=THT]
  R3 = Resistor [tolerance=±5% resistance=220 package=THT]
  R4 = Resistor [tolerance=±5% resistance=220 package=THT]
  R1 = Resistor [tolerance=±5% resistance=220 package=THT]
  LED1 = LED - 3mm [color="Red (633nm)" package="3 mm [THT]"]
  LED2 = LED - 3mm [color="Red (633nm)" package="3 mm [THT]"]
  LED3 = LED - 3mm [color="Red (633nm)" package="3 mm [THT]"]
  LED4 = LED - 3mm [color="Red (633nm)" package="3 mm [THT]"]
  JP1 = Jumper [package=sj_2s-no-ns]

nets:
  3V3: Raspberry_Pi_Zero1.3v3, Raspberry_Pi_Zero1.3V3, 4_Channel_Relay1.COM
  GND: Raspberry_Pi_Zero1.GND, 4_Channel_Relay1.GND, LED1.cathode, LED2.cathode, LED3.cathode, LED4.cathode
  N1: Raspberry_Pi_Zero1.GPIO17, 4_Channel_Relay1.IN1
  N2: Raspberry_Pi_Zero1.GPIO27, 4_Channel_Relay1.IN2
  N3: Raspberry_Pi_Zero1.GPIO22, 4_Channel_Relay1.IN3
  N4: Raspberry_Pi_Zero1.GPIO23, 4_Channel_Relay1.IN4
  N5: Raspberry_Pi_Zero1.5V, 4_Channel_Relay1.VCC#13
  N6: 4_Channel_Relay1.VCC#14, JP1.1
  N7: 4_Channel_Relay1.JD-VCC, JP1.2
  N8: 4_Channel_Relay1.NO#18, R4.Pin_0
  N9: 4_Channel_Relay1.NO#21, R3.Pin_0
  N10: 4_Channel_Relay1.NO#24, R2.Pin_0
  N11: 4_Channel_Relay1.NO#27, R1.Pin_0
  N12: R2.Pin_1, LED2.anode
  N13: R3.Pin_1, LED3.anode
  N14: R4.Pin_1, LED4.anode
  N15: R1.Pin_1, LED1.anode

custom parts:
  4 Channel Power Relay: A 4 channel power relay. The module operates at 5V.
